# Fritzing sketch Sketch (saved by Fritzing 0.9.5d)

parts:
  S1 = H-Bridge with L298N
  LED1 = LED - 5mm [color="White (4500K)" package="5 mm [THT]"]  # not connected
  Part1 = HC-SR501 Body Sensor Module  # not connected
  M1 = DC Motor
  VCC1 = Battery block 9V

nets:
  N1: S1.12V, VCC1.+
  N2: S1.GND, S1.IN2, VCC1.-
  N3: S1.ENA, S1.ENA-5V
  N4: S1.ENB, S1.ENB-5V
  N5: S1.M1-01, M1.pin_2
  N6: S1.M1-02, M1.pin_1

notes:
  USB-6255
  Images are for illustrative purposes only
  AI 0
  AI GND
  AO GND
  AO 0
  5v+
  AO 1

custom parts:
  H-Bridge with L298N: h-bridge
  HC-SR501 Body Sensor Module: Pyroelectric Infrared PIR Motion Sensor Detector Module
